# Fritzing sketch sunriseMachine (saved by Fritzing 0.9.3b)
breadboards: 1

parts:
  Part9 = Tessel 2
  S1 = Pushbutton [package="[THT]"]
  LED1 = RGB LED (com. cathode, rgb) [package="5 mm [THT]"]
  R1 = Resistor [tolerance=±5% resistance=100 package=THT]
  R2 = Resistor [tolerance=±5% resistance=10k package=THT]

nets:
  N1: Part9.GND, R1.Pin_1, R2.Pin_1
  N2: Part9.3V3, S1.Pin_3, S1.Pin_4
  N3: Part9.2, S1.Pin_1, S1.Pin_2, R2.Pin_0
  N4: Part9.5#35, LED1.blue_anode
  N5: Part9.6, LED1.common_cathode
  N6: Part9.5#75, LED1.red_anode
  N7: LED1.green_anode, R1.Pin_0

notes:
  Plug a USB thumb drive and a USB webcam into the Tessel 2's USB ports

custom parts:
  Tessel 2: Draft version of Tessel 2
